// Logisim project hw3.circ as structural Verilog: 7 circuits, main circuit CPU
module CPU (
);

  wire clk_out, main_ctrl_1_alusrc, main_ctrl_1_beq, main_ctrl_1_bne, main_ctrl_1_extop, main_ctrl_1_j,
       main_ctrl_1_memread, main_ctrl_1_memtoreg, main_ctrl_1_memwrite, main_ctrl_1_regwrite, nextpc_1_pcsrc,
       registerfile_1_p3, registerfile_1_p7;
  wire [3:0] alu_ctrl_1_aluop;
  wire [4:0] mipsprogramrom_1_p2_2, mipsprogramrom_1_p2_3, mipsprogramrom_1_p2_4, mipsprogramrom_1_p2_5,
       multiplexer_2_out;
  wire [5:0] mipsprogramrom_1_p2, mipsprogramrom_1_p2_6;
  wire [19:0] mips_alu_1_p5;
  wire [29:0] incrementer_1_p1, nextpc_1_address;
  wire [31:0] extender_1_imm32, mips_ram_1_p6, multiplexer_3_out, PC_q, registerfile_1_p1, registerfile_1_p8;
  wire [31:2] multiplexer_1_out;
  wire [31:20] mips_alu_1_p5_2;

  Multiplexer #(.width(30), .enable("false")) multiplexer_1 (
    .in0(incrementer_1_p1), .in1(nextpc_1_address), .out(multiplexer_1_out), .sel(nextpc_1_pcsrc));
  Clock clk (.out(clk_out));
  Register #(.width(32), .trigger("falling")) PC (
    .D({multiplexer_1_out, 2'b00}), .en(1'b1), .clk(clk_out), .Q(PC_q));  // open: clr
  // Incrementer #(.width(30)) incrementer_1: pin names not known; wires that end beside it: incrementer_1_p1, PC_q[31:2]
  // MIPSProgramROM mipsprogramrom_1: pin names not known; wires that end beside it: PC_q, {mipsprogramrom_1_p2_6, mipsprogramrom_1_p2_5, mipsprogramrom_1_p2_4, mipsprogramrom_1_p2_3, mipsprogramrom_1_p2_2, mipsprogramrom_1_p2}
  Multiplexer #(.width(5), .enable("false")) multiplexer_2 (
    .in0(mipsprogramrom_1_p2_3), .in1(mipsprogramrom_1_p2_4), .out(multiplexer_2_out),
    .sel(main_ctrl_1_regwrite));
  // RegisterFile #(.trigger("falling")) registerfile_1: pin names not known; wires that end beside it: registerfile_1_p1, clk_out, registerfile_1_p3, multiplexer_2_out, mipsprogramrom_1_p2_2, mipsprogramrom_1_p2_3, registerfile_1_p7, registerfile_1_p8
  main_ctrl main_ctrl_1 (
    .I5(mipsprogramrom_1_p2[5]), .I4(mipsprogramrom_1_p2[4]), .I3(mipsprogramrom_1_p2[3]),
    .I2(mipsprogramrom_1_p2[2]), .I1(mipsprogramrom_1_p2[1]), .I0(mipsprogramrom_1_p2[0]),
    .RegDst(registerfile_1_p3), .RegWrite(main_ctrl_1_regwrite), .ExtOp(main_ctrl_1_extop),
    .ALUSrc(main_ctrl_1_alusrc), .Beq(main_ctrl_1_beq), .Bne(main_ctrl_1_bne), .J(main_ctrl_1_j),
    .MemRead(main_ctrl_1_memread), .MemWrite(main_ctrl_1_memwrite), .MemtoReg(main_ctrl_1_memtoreg));
  extender extender_1 (
    .ExtOp(main_ctrl_1_extop), .Imm16({mipsprogramrom_1_p2_3, mipsprogramrom_1_p2_2, mipsprogramrom_1_p2}),
    .Imm32(extender_1_imm32));
  Multiplexer #(.width(32), .enable("false")) multiplexer_3 (
    .in0(registerfile_1_p8), .in1(extender_1_imm32), .out(multiplexer_3_out), .sel(main_ctrl_1_alusrc));
  alu_ctrl alu_ctrl_1 (.func(mipsprogramrom_1_p2_6), .opcode(mipsprogramrom_1_p2), .ALUop(alu_ctrl_1_aluop));
  // Mips_ALU mips_alu_1: pin names not known; wires that end beside it: registerfile_1_p7, multiplexer_3_out, alu_ctrl_1_aluop, mipsprogramrom_1_p2_5, {mips_alu_1_p5_2, mips_alu_1_p5}
  nextpc nextpc_1 (
    .J(main_ctrl_1_j), .BNE(main_ctrl_1_bne), .PCSRC(nextpc_1_pcsrc),
    .ZERO({mips_alu_1_p5_2, mips_alu_1_p5}), .INC_PC(incrementer_1_p1), .BEQ(main_ctrl_1_beq),
    .IMM26({mipsprogramrom_1_p2_5, mipsprogramrom_1_p2_4, mipsprogramrom_1_p2_3, mipsprogramrom_1_p2_2, mipsprogramrom_1_p2}),
    .ADDRESS(nextpc_1_address));
  // MIPS_RAM mips_ram_1: pin names not known; wires that end beside it: mips_alu_1_p5, registerfile_1_p8, main_ctrl_1_memwrite, clk_out, main_ctrl_1_memread, mips_ram_1_p6, {mips_alu_1_p5_2, mips_alu_1_p5}
  Multiplexer #(.width(32), .enable("false")) multiplexer_4 (
    .in0({mips_alu_1_p5_2, mips_alu_1_p5}), .in1(mips_ram_1_p6), .out(registerfile_1_p1),
    .sel(main_ctrl_1_memtoreg));

  // Notes on the sheet:
  //   contents of mipsprogramrom_1 (hex, n*v repeats v):
  //   addiu $s0, $s1, 16 lw $t5, 0($t5) j foo  foo: beq $t0, $s2, end  end: sw $t0, 0($s5) xor $v0, $t3,
  //   $s5 sll $t4, $t1, 2
endmodule

module nextpc (
  input  [29:0] INC_PC,
  input  BEQ,
  input  BNE,
  input  J,
  input  [25:0] IMM26,
  input  [31:0] ZERO,
  output PCSRC,
  output [29:0] ADDRESS
);

  wire and_1_out, and_2_out, comparator_1_eq;
  wire [29:0] adder_1_out, bit_extender_1_out;

  assign bit_extender_1_out = {{14{IMM26[15]}}, IMM26[15:0]};  // Bit_Extender bit_extender_1
  Adder #(.width(30)) adder_1 (.a(INC_PC), .b(bit_extender_1_out), .out(adder_1_out));  // open: cin, cout
  Multiplexer #(.width(30), .enable("false")) multiplexer_1 (
    .in0(adder_1_out), .in1({INC_PC[29:26], IMM26}), .out(ADDRESS), .sel(J));
  and and_1 (and_1_out, ~comparator_1_eq, BNE);  // AND_Gate
  Comparator #(.width(32)) comparator_1 (.a({32{1'b0}}), .b(ZERO), .eq(comparator_1_eq));  // open: gt, lt
  or or_1 (PCSRC, and_1_out, J, and_2_out);
  and and_2 (and_2_out, comparator_1_eq, BEQ);
endmodule

module alu_r_tip (
  input  i5,
  input  I4,
  input  I3,
  input  I2,
  input  I1,
  input  I0,
  output O3,
  output O2,
  output O1,
  output O0
);

  wire not_1_out;

  and and_1 (O1, i5, I0);
  not not_1 (not_1_out, i5);
  and and_2 (O0, not_1_out, I0);

  assign O2 = I1;
  assign O3 = I2;
endmodule

module alu_i_tip (
  input  I5,
  input  I4,
  input  I3,
  input  I2,
  input  I1,
  input  I0,
  output O3,
  output O2,
  output O1,
  output O0
);

  wire and_2_out, and_3_out, not_1_out, not_2_out, not_3_out, not_4_out;

  and and_1 (O3, I3, I2);
  not not_1 (not_1_out, I3);
  not not_2 (not_2_out, I1);
  not not_3 (not_3_out, I0);
  not not_4 (not_4_out, I3);
  and and_2 (and_2_out, not_1_out, not_2_out);
  and and_3 (and_3_out, I1, not_3_out);
  or or_1 (O1, not_4_out, I0);
  or or_2 (O2, and_2_out, and_3_out);

  assign O0 = 1'b0;
endmodule

module alu_ctrl (
  input  [5:0] func,
  input  [5:0] opcode,
  output [3:0] ALUop
);

  wire comparator_1_eq, not_1_out;
  wire [3:0] alu_i_tip_1_o0, alu_r_tip_1_o0;

  Comparator #(.width(6)) comparator_1 (.a(func), .b({6{1'b0}}), .eq(comparator_1_eq));  // open: gt, lt
  alu_r_tip alu_r_tip_1 (
    .i5(func[5]), .I4(func[4]), .I3(func[3]), .I2(func[2]), .I1(func[1]), .I0(func[0]),
    .O3(alu_r_tip_1_o0[3]), .O2(alu_r_tip_1_o0[2]), .O1(alu_r_tip_1_o0[1]), .O0(alu_r_tip_1_o0[0]));
  alu_i_tip alu_i_tip_1 (
    .I5(opcode[5]), .I4(opcode[4]), .I3(opcode[3]), .I2(opcode[2]), .I1(opcode[1]), .I0(opcode[0]),
    .O3(alu_i_tip_1_o0[3]), .O2(alu_i_tip_1_o0[2]), .O1(alu_i_tip_1_o0[1]), .O0(alu_i_tip_1_o0[0]));
  not not_1 (not_1_out, comparator_1_eq);
  Multiplexer #(.width(4), .enable("false")) multiplexer_1 (
    .in0(alu_r_tip_1_o0), .in1(alu_i_tip_1_o0), .out(ALUop), .sel(not_1_out));
endmodule

module main_ctrl (
  input  I5,
  input  I4,
  input  I3,
  input  I2,
  input  I1,
  input  I0,
  output RegDst,
  output RegWrite,
  output ExtOp,
  output ALUSrc,
  output Beq,
  output Bne,
  output J,
  output MemRead,
  output MemWrite,
  output MemtoReg
);

  wire and_3_out, and_4_out, and_5_out, not_1_out, not_2_out, not_3_out, not_4_out, not_5_out, not_6_out,
       not_8_out, not_9_out, not_10_out, not_11_out, not_12_out, not_13_out, not_14_out;

  not not_1 (not_1_out, I3);
  not not_2 (not_2_out, I0);
  not not_3 (not_3_out, I2);
  not not_4 (not_4_out, I1);
  not not_5 (not_5_out, I5);
  not not_6 (not_6_out, I3);
  not not_7 (ExtOp, I2);
  or or_1 (ALUSrc, I1, I3);
  not not_8 (not_8_out, I3);
  not not_9 (not_9_out, I0);
  not not_10 (not_10_out, I3);
  not not_11 (not_11_out, I1);
  not not_12 (not_12_out, I3);
  not not_13 (not_13_out, I0);
  not not_14 (not_14_out, I3);
  and and_1 (MemWrite, I5, I3);
  and and_2 (RegDst, not_1_out, not_2_out);
  and and_3 (and_3_out, not_3_out, not_4_out);
  and and_4 (and_4_out, not_5_out, I3);
  and and_5 (and_5_out, I5, not_6_out);
  and and_6 (Beq, not_8_out, I2, not_9_out);
  and and_7 (Bne, not_10_out, not_11_out, I0);
  and and_8 (J, not_12_out, I1, not_13_out);
  and and_9 (MemRead, I5, not_14_out);
  or or_2 (RegWrite, and_3_out, and_4_out, and_5_out);

  assign MemtoReg = I5;
endmodule

module extender (
  input  ExtOp,
  input  [15:0] Imm16,
  output [31:0] Imm32
);

  and and_1 (Imm32[31], ExtOp, Imm16[15]);

  assign Imm32[30:0] = {{15{Imm32[31]}}, Imm16};
endmodule
